// Logisim project lab1_2.circ as structural Verilog: 1 circuit, main circuit main
module main (
  input  A2,
  input  A1,
  input  B2,
  input  B1,
  output C1,
  output C2
);

  wire and_1_out, and_3_out, nand_1_out, nand_2_out, not_1_out, or_1_out, or_2_out, or_3_out, xor_1_out,
       xor_2_out;

  not not_1 (not_1_out, B2);
  xor xor_1 (xor_1_out, A2, not_1_out);
  nand nand_1 (nand_1_out, A2, B1);
  nand nand_2 (nand_2_out, A1, B2);
  and and_1 (and_1_out, xor_1_out, A1);
  xor xor_2 (xor_2_out, A1, B1);
  or or_1 (or_1_out, nand_2_out, B1);
  or or_2 (or_2_out, A2, B2);
  or or_3 (or_3_out, A1, nand_1_out);
  or or_4 (C1, and_1_out, xor_2_out);
  and and_2 (C2, or_1_out, and_3_out);
  and and_3 (and_3_out, or_2_out, or_3_out);
endmodule
