// Logisim project lab2.circ as structural Verilog: 1 circuit, main circuit main
module main (
  input  A1,
  input  A0,
  input  B1,
  input  S0,
  input  B0,
  input  S1,
  output C2,
  output C1,
  output C0
);

  wire and_1_out, and_2_out, and_3_out, n4_to_1_mux_x2_74153_1_p5, n4_to_1_mux_x2_74153_1_p9, not_1_out,
       xor_1_out, xor_2_out;

  xor xor_1 (xor_1_out, A0, B0);
  not not_1 (not_1_out, 1'b1);
  // _4_to_1_MUX__x2___74153 #(.Facing("east")) 4_to_1_mux_x2_74153_1: pin names not known; wires that end beside it: A0, 1'b1, A1, B1, n4_to_1_mux_x2_74153_1_p5, 1'b1, A0, B0, n4_to_1_mux_x2_74153_1_p9, not_1_out, S0, not_1_out, S1, C2, C1
  // _4_to_1_MUX__x2___74153 #(.Facing("east")) 4_to_1_mux_x2_74153_2: pin names not known; wires that end beside it: not_1_out, not_1_out, 1'b1, xor_1_out, not_1_out, S0, S1, C0
  and and_1 (and_1_out, B0, A0);
  xor xor_2 (xor_2_out, A1, B1);
  xor xor_3 (n4_to_1_mux_x2_74153_1_p9, xor_2_out, and_1_out);
  and and_2 (and_2_out, xor_2_out, and_1_out);
  and and_3 (and_3_out, B1, A1);
  or or_1 (n4_to_1_mux_x2_74153_1_p5, and_2_out, and_3_out);
endmodule
